# Fritzing sketch smartcardiagram (saved by Fritzing 0.9.3b)

parts:
  Part1 = Arduino Uno (Rev3)
  J1 = Basic Servo
  J2 = Basic Servo
  Keyes1 = Keyes IR Infrared Sensor Switch Module
  U1 = NodeMCU V1.0
  Keyes2 = Keyes IR Infrared Sensor Switch Module
  Keyes3 = Keyes IR Infrared Sensor Switch Module
  Keyes4 = Keyes IR Infrared Sensor Switch Module
  Keyes5 = Keyes IR Infrared Sensor Switch Module
  Keyes6 = Keyes IR Infrared Sensor Switch Module
  Keyes7 = Keyes IR Infrared Sensor Switch Module
  Keyes8 = Keyes IR Infrared Sensor Switch Module

nets:
  N1: Part1.D8, Keyes4.out
  N2: Part1.D9_PWM, Keyes3.out
  N3: Part1.D10_PWM/SS, Keyes5.out
  N4: Part1.D11_PWM/MOSI, Keyes1.out
  N5: Part1.D12/MISO, Keyes7.EN
  N6: Part1.D13/SCK, J1.pulse
  N7: Part1.D0/RX, U1.TX
  N8: Part1.D1/TX, U1.RX
  N9: Part1.D3_PWM, J2.pulse
  N10: Part1.D4, Keyes8.out
  N11: Part1.D6_PWM, Keyes2.out
  N12: Part1.D7, Keyes6.out
  5V: Part1.5V, Keyes1.VCC
  GND: Part1.GND, Keyes1.GND

custom parts:
  Keyes IR Infrared Sensor Switch Module: An infrared obstacle detector
  NodeMCU V1.0: ESP8266 based NodeMCU
